// Logisim project mwm21cAssg7.circ as structural Verilog: 1 circuit, main circuit main
module main (
  input  A,
  input  B,
  input  C,
  output F,
  output E,
  output D
);

  wire and_1_out, and_2_out, and_3_out, not_1_out, not_2_out, not_3_out;

  and and_1 (and_1_out, A, B, not_1_out);
  not not_1 (not_1_out, C);
  not not_2 (not_2_out, A);
  and and_2 (and_2_out, not_2_out, B, C);
  and and_3 (and_3_out, A, B, not_3_out);
  not not_3 (not_3_out, C);
  and and_4 (F, A, B, C);
  or or_1 (D, A, B, C);
  or or_2 (E, and_1_out, and_2_out, and_3_out);
endmodule
